# Fritzing sketch Breadboard Fritzing Soar (saved by Fritzing 0.9.4)
breadboards: 1

parts:
  Teensy1 = Teensy 3.6 (Basic)
  Part1 = MPL3115A2 I2C Barometric Pressure, Altitude, Temperature Sensor
  LSM9DS1 = SparkFun-LSM9DS1-Breakout [part_number=SEN-13284]
  R2 = Resistor [tolerance=±20% resistance=10k package="2010 [SMD]"]
  R5 = Resistor [tolerance=±5% resistance=10k package="1206 [SMD]"]
  R6 = Resistor [tolerance=±10% resistance=10k package="0805 [SMD]"]
  R7 = Resistor [tolerance=±5% resistance=10k package="0805 [SMD]"]
  R8 = Resistor [tolerance=±5% resistance=10k package="0805 [SMD]"]
  R9 = Resistor [tolerance=±5% resistance=10k package="0805 [SMD]"]
  R10 = Resistor [tolerance=±5% resistance=10k package="0805 [SMD]"]
  R11 = Resistor [tolerance=±5% resistance=10k package="0805 [SMD]"]
  R12 = PHOTOCELL [package=photocell]
  R13 = PHOTOCELL [package=photocell]
  R14 = PHOTOCELL [package=photocell]
  R15 = PHOTOCELL [package=photocell]
  R17 = Temperature Sensor (Thermistor) [thermistor_type=NTC package=THT]
  R18 = Temperature Sensor (Thermistor) [thermistor_type=NTC package=THT]
  R19 = Temperature Sensor (Thermistor) [thermistor_type=NTC package=THT]
  R20 = Temperature Sensor (Thermistor) [thermistor_type=NTC package=THT]
  R21 = Temperature Sensor (Thermistor) [thermistor_type=NTC package=THT]
  R22 = Resistor [tolerance=±5% resistance=10k package="0805 [SMD]"]
  BAT1 = Battery Holders [package=battery-aa]

nets:
  GND: Teensy1.GND, Teensy1.GND1, Part1.GND, LSM9DS1.GND, R2.Pin_1, R5.Pin_1, R6.Pin_1, R7.Pin_1, R17.pin_1, R18.pin_1, R19.pin_1, R20.pin_1, R21.pin_1, BAT1.+
  N1: Teensy1.D3, Part1.SCL
  N2: Teensy1.D4, Part1.SDA
  N3: Teensy1.A4/D18, LSM9DS1.SDA
  N4: Teensy1.A5/D19, LSM9DS1.SCL
  N5: Teensy1.3V3, Teensy1.3V3_1
  N6: Teensy1.D31, R2.Pin_0, R15.P$2
  N7: Teensy1.D32, R5.Pin_0, R13.P$2
  N8: Teensy1.D33, R6.Pin_0, R14.P$2
  N9: Teensy1.D34, R7.Pin_0, R12.P$2
  N10: Teensy1.D35, R8.Pin_1, R20.pin_0
  N11: Teensy1.D36, R9.Pin_1, R19.pin_0
  N12: Teensy1.D37, R10.Pin_1, R17.pin_0
  N13: Teensy1.D38, R11.Pin_1, R18.pin_0
  N14: Teensy1.D39, R21.pin_0, R22.Pin_1
  VIN: Part1.VIN, LSM9DS1.VDD, R8.Pin_0, R9.Pin_0, R10.Pin_0, R11.Pin_0, R12.P$1, R13.P$1, R14.P$1, R15.P$1, R22.Pin_0, BAT1.-

custom parts:
  Teensy 3.6 (Basic): The Teensy is a complete USB-based microcontoller development system, in a very small footprint, capable of implementing many types of projects. All programming is done via the USB port. No special programmer is needed, only a standard micro-USB cable and a PC or Macintosh with a USB port.
  MPL3115A2 I2C Barometric Pressure, Altitude, Temperature Sensor: This pressure sensor from Freescale is a great low-cost sensing solution for precision measurement of barometric pressure and altitude. The MPL3115A2 has a typical 1.5 Pascal resolution, which can resolve altitude at 0.3 meters (compare to the BMP180 which can do 0.17m). It has some upsides compared to the BMP180, such as interrupt outputs for ultra-low power usage, and its also a heck of a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
  SparkFun-LSM9DS1-Breakout: The LSM9DS1 is a versatile, motion-sensing system-in-a-chip. It houses a 3-axis accelerometer, 3-axis gyroscope, and 3-axis magnetometer – nine degrees of freedom (9DOF) in a single IC! The LSM9DS1 is equipped with a digital interface, but even that is flexible: it supports both I2C and SPI, so you’ll be hard-pressed to find a microcontroller it doesn’t work with. Each sensor in the LSM9DS1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
